# Fritzing sketch module 4 relay 5v (saved by Fritzing 0.9.3b)

parts:
  4_Relay_Module_5V = Module 4 Relais 5V [package="Module 4 Relais 5V"]
  Raspberry_Pi_2 = Raspberry Pi 2

nets:
  VCC: 4_Relay_Module_5V.VCC, Raspberry_Pi_2.5V
  GND: 4_Relay_Module_5V.GND, Raspberry_Pi_2.GND
  N1: 4_Relay_Module_5V.IN1, Raspberry_Pi_2.GPIO2
  N2: 4_Relay_Module_5V.IN2, Raspberry_Pi_2.GPIO3
  N3: 4_Relay_Module_5V.IN3, Raspberry_Pi_2.GIPO4
  N4: 4_Relay_Module_5V.IN4, Raspberry_Pi_2.ID_SC

notes:
  Kalifiabillal@gmail.com

custom parts:
  Module 4 Relais 5V: Module 4 Relais 5V 4x SPD-06VDC-SD-C
